// Logisim project SMART HOME SECURITY SYSTEM.circ as structural Verilog: 1 circuit, main circuit main
module main (
  input  FRONT_DOOR,
  input  BACK_DOOR,
  input  WINDOW,
  input  MOTION,
  input  ARMED_HOME,
  input  MOTION_2,
  input  ARMED_HOME_2,
  input  IS_NIGHT,
  input  SMOKESENSOR,
  output ALERT
);

  wire AND_2_out, AND_out, OR_out;

  or OR (OR_out, FRONT_DOOR, BACK_DOOR, WINDOW);
  and AND (AND_out, MOTION, ARMED_HOME);
  and AND_2 (AND_2_out, MOTION_2, ARMED_HOME_2, IS_NIGHT);
  or OR_2 (ALERT, OR_out, AND_out, AND_2_out, SMOKESENSOR);
endmodule
